// Logisim project FetchDesign5.circ as structural Verilog: 2 circuits, main circuit main
module main (
  input  [2:0] Value_4,
  input  [31:0] Initialise,
  input  [31:0] Immediate_Value,
  input  [31:0] Return_Address,
  input  S1,
  input  in_6,
  input  S0,
  output [31:0] MAR
);

  wire clock_1_out;
  wire [31:0] adder_1_out, bit_extender_1_out, mux_1_o, mux_2_o, PC_q;

  MUX mux_1 (.A(Initialise), .B(Return_Address), .S(S0), .O(mux_1_o));
  Clock clock_1 (.out(clock_1_out));
  Register #(.width(32)) PC (.D(mux_1_o), .Q(PC_q), .clk(clock_1_out), .clr(in_6));  // open: en
  assign bit_extender_1_out = {{29{1'b0}}, Value_4};  // Bit_Extender bit_extender_1
  MUX mux_2 (.A(Immediate_Value), .B(bit_extender_1_out), .S(S1), .O(mux_2_o));
  Adder #(.width(32)) adder_1 (.a(mux_2_o), .b(PC_q), .out(adder_1_out));  // open: cin, cout
  MUX mux_3 (.A(adder_1_out), .B(Return_Address), .S(S0), .O(MAR));
endmodule

module MUX (
  input  [31:0] A,
  input  [31:0] B,
  input  S,
  output [31:0] O
);

  wire [31:0] and_1_out, and_2_out, bit_extender_1_out, not_1_out;

  assign bit_extender_1_out = {{31{S}}, S};  // Bit_Extender bit_extender_1
  assign not_1_out = ~bit_extender_1_out;  // NOT_Gate not_1, 32 bits wide
  assign and_1_out = A & not_1_out;  // AND_Gate and_1, 32 bits wide
  assign and_2_out = B & bit_extender_1_out;  // AND_Gate and_2, 32 bits wide
  assign O = and_1_out | and_2_out;  // OR_Gate or_1, 32 bits wide
endmodule
